// Logisim project y86.circ as structural Verilog
module main (
  input  Reset,
  output [3:0] out_2,
  output [3:0] out_3,
  output [3:0] out_4,
  output [3:0] out_5,
  output [31:0] out_6,
  output [31:0] out_7,
  output [31:0] out_8,
  output [31:0] out_9,
  output [31:0] out_10,
  output [31:0] out_11,
  output [31:0] out_12,
  output [31:0] out_13,
  output [31:0] out_14,
  output [31:0] out_15,
  output [31:0] out_16,
  output [31:0] out_17,
  output [31:0] out_18,
  output out_19,
  output out_20,
  output out_21
);

  wire and_1_out, and_2_out, Clock_out, dmemError, imemError, need_reg_1_needregs, nor_1_out, not_1_out,
       not_2_out, not_3_out, not_4_out, ofl, select_read_read, select_write_write, setcc, sfl, zfl;
  wire [1:0] Stat_q, Status_Update_new_stat;
  wire [3:0] select_dstE_deste, select_dstM_dst_m, select_srcA_srca, select_srcB_out_3;
  wire [7:0] imem_1_p5, imem_1_p6, imem_1_p7, imem_1_p8, imem_1_p9, imem_1_p10, imem_1_p11, imem_1_p12,
       imem_1_p13;
  wire [31:0] pc_increment_1_new_pc, PC_q, select_address_address_0, select_address_address_1,
       select_aluA_alua_0, select_aluA_alua_1, select_aluB_alub_0, select_aluB_alub_1, select_data_data_0,
       select_data_data_1, valP;

  and and_1 (and_1_out, Clock_out, nor_1_out);
  Clock Clock (.out(Clock_out));
  Register #(.width(32)) PC (.D(out_14), .Q(PC_q), .clk(and_1_out), .clr(Reset));  // open: en
  nor nor_1 (nor_1_out, Stat_q[1], Stat_q[0]);
  not not_1 (not_1_out, and_1_out);
  Register #(.width(2)) Stat (.D(Status_Update_new_stat), .Q(Stat_q), .clk(not_1_out));  // open: en, clr
  LED led_1 (.in(imemError));
  // imem imem_1: pin names not known; wires that end beside it: out_14, PC_q, imemError, {out_2, out_3}, imem_1_p5, imem_1_p6, imem_1_p7, imem_1_p8, imem_1_p9, imem_1_p10, imem_1_p11, imem_1_p12, imem_1_p13
  Align align_1 (
    .B1(imem_1_p5), .B2(imem_1_p6), .B3(imem_1_p7), .B4(imem_1_p8), .B5(imem_1_p9), .B6(imem_1_p10),
    .B7(imem_1_p11), .B8(imem_1_p12), .B9(imem_1_p13), .needReg(need_reg_1_needregs), .valC_1(out_7),
    .rB(out_5), .rA(out_4), .valC_0(out_6));
  need_reg need_reg_1 (.icode(out_2), .NeedRegs(need_reg_1_needregs));
  LED led_2 (.in(not_1_out));
  not not_2 (not_2_out, not_1_out);
  not not_3 (not_3_out, not_1_out);
  LED led_3 (.in(not_2_out));
  LED led_4 (.in(not_3_out));
  LED led_5 (.in(not_1_out));
  Status_Update Status_Update (
    .icode(out_2), .new_stat(Status_Update_new_stat), .dmemError(dmemError), .imemError(imemError),
    .ifun(out_3));
  LED led_6 (.in(dmemError));
  srcA select_srcA (.rA(out_4), .icode(out_2), .srcA(select_srcA_srca));
  srcB select_srcB (.rB(out_5), .in_1(out_2), .out_3(select_srcB_out_3));
  dstE select_dstE (
    .destE(select_dstE_deste), .icode(out_2), .rB(out_5), .ifun(out_3), .zf(out_20), .sf(out_19), .of(out_21));
  dstM select_dstM (.rA(out_4), .icode(out_2), .dst_M(select_dstM_dst_m));
  LED led_7 (.in(not_1_out));
  not not_4 (not_4_out, not_1_out);
  LED led_8 (.in(not_4_out));
  // regfile regfile_1: pin names not known; wires that end beside it: select_srcA_srca, select_srcB_out_3, select_dstE_deste, out_13, out_12, select_dstM_dst_m, out_18, out_17, not_1_out, Reset, out_9, out_8, out_11, out_10
  select_aluA select_aluA (
    .icode(out_2), .icode_2(out_2), .aluA_0(select_aluA_alua_0), .aluA_1(select_aluA_alua_1), .valA_0(out_8),
    .valA_1(out_9), .valC_0(out_6), .valC_1(out_7));
  select_aluB select_aluB (
    .icode(out_2), .aluB_0(select_aluB_alub_0), .icode_2(out_2), .aluB_1(select_aluB_alub_1),
    .valB_0(out_10), .valB_1(out_11));
  alu ALU (
    .aluA_1(select_aluA_alua_1), .aluA_0(select_aluA_alua_0), .aluB_1(select_aluB_alub_1),
    .aluB_0(select_aluB_alub_0), .out_6(zfl), .out_7(sfl), .out_8(ofl), .ALUfun(out_3), .valE_1(out_13),
    .valE_0(out_12));
  select_read select_read (.icode(out_2), .read(select_read_read));
  select_write select_write (.icode(out_2), .write(select_write_write));
  select_address select_address (
    .address_0(select_address_address_0), .address_1(select_address_address_1), .icode_2(out_2),
    .icode(out_2), .valE_0(out_12), .valE_1(out_13), .valA_0(out_8), .valA_1(out_9));
  select_data select_data (
    .icode(out_2), .icode_2(out_2), .data_1(select_data_data_1), .data_0(select_data_data_0), .valP_0(valP),
    .valA_0(out_8), .valA_1(out_9));
  // dmem dmem_1: pin names not known; wires that end beside it: select_address_address_1, select_address_address_0, select_data_data_1, select_data_data_0, select_read_read, select_write_write, dmemError, not_1_out, Reset, out_18, out_17, {ofl, sfl, zfl}
  PC_Increment pc_increment_1 (
    .icode(out_2), .ifun(out_3), .PC(PC_q), .zf(out_20), .sf(out_19), .of(out_21), .valC(out_6),
    .valM(out_17), .New_PC(pc_increment_1_new_pc), .valP(valP));
  and and_2 (and_2_out, setcc, not_1_out);
  Register #(.width(3)) register_1 (
    .D({ofl, sfl, zfl}), .Q({out_21, out_19, out_20}), .clk(and_2_out), .clr(Reset));  // open: en
  Register #(.width(32)) PChold (.D(pc_increment_1_new_pc), .Q(out_14), .clk(not_1_out), .clr(Reset));  // open: en
  Multiplexer #(.select(4), .enable("false")) multiplexer_1 (
    .in0(1'b0), .in1(1'b0), .in2(1'b0), .in3(1'b0), .in4(1'b0), .in5(1'b0), .in6(1'b1), .in7(1'b0),
    .in8(1'b0), .in9(1'b0), .in10(1'b0), .in11(1'b0), .out(setcc), .sel(out_2));  // open: in12, in13, in14, in15

  // Other names for the same wires on the sheet: ifun[3:0] = out_3; icode[3:0] = out_2; zf = out_20; sf = out_19;
  //   of = out_21; memory_address_0[31:0] = out_15; memory_address_1[31:0] = out_16; new_PC[31:0] = out_14;
  //   rA[3:0] = out_4; rB[3:0] = out_5; valA_0[31:0] = out_8; valA_1[31:0] = out_9; valB_0[31:0] = out_10;
  //   valB_1[31:0] = out_11; valC_0[31:0] = out_6; valC_1[31:0] = out_7; valE_0[31:0] = out_12; valE_1[31:0] = out_13;
  //   valM_0[31:0] = out_17; valM_1[31:0] = out_18

  // Notes on the sheet:
  //   Fetch Stage:
  //   rA, rB, valC,
  //   and valP
  //   imemError
  //   icode, ifun,
  //   are computed.
  //   dmemError
  //   Decode stage:
  //   srcA and srcB
  //   are found based 
  //   on the icode.
  //   From srcA and srcB
  //   valA and valB are
  //   computed.
  //   Execute Stage:
  //   The core instruction is executed,
  //   computing valE and condition codes.
  //   PC Update stage:
  //   The held value in the program counter hold
  //   is sent to the program counter.
  //   output valM.
  //   Memory and Writeback:
  //   Read or write to memory based
  //   on instruction content and
  //   PC Inc
endmodule

module Align (
  input  [7:0] B1,
  input  [7:0] B2,
  input  [7:0] B3,
  input  [7:0] B4,
  input  [7:0] B5,
  input  [7:0] B6,
  input  [7:0] B7,
  input  [7:0] B8,
  input  [7:0] B9,
  input  needReg,
  output [31:0] valC_0,
  output [3:0] rB,
  output [3:0] rA,
  output [31:0] valC_1
);

  Multiplexer #(.width(32), .enable("false")) multiplexer_1 (
    .in0({B4, B3, B2, B1}), .in1({B5, B4, B3, B2}), .out(valC_0), .sel(needReg));
  Multiplexer #(.width(32), .enable("false")) multiplexer_2 (
    .in0({B8, B7, B6, B5}), .in1({B9, B8, B7, B6}), .out(valC_1), .sel(needReg));

  assign rA = B1[7:4];
  assign rB = B1[3:0];

  // Other names for the same wires on the sheet: need_regs = needReg

  // Notes on the sheet:
  //   switch these based on endianess
  //   valC_0 is lower 32 bits, while valC_1 is upper 32, more significant, bits
endmodule

module PC_Increment (
  input  [3:0] icode,
  input  [3:0] ifun,
  input  [31:0] PC,
  input  zf,
  input  sf,
  input  of,
  input  [31:0] valC,
  input  [31:0] valM,
  output [31:0] valP,
  output [31:0] New_PC
);

  wire multiplexer_3_out, n1_jle_1_out_4, n5_jge_1_out_3, n6_jg_1_out_4, not_1_out, undriven;
  wire [31:0] multiplexer_1_out, multiplexer_2_out;

  Multiplexer #(.select(4), .width(32), .enable("false")) multiplexer_1 (
    .in0(32'h1), .in1(32'h1), .in2(32'h2), .in3(32'ha), .in4(32'ha), .in5(32'ha), .in6(32'h2), .in7(32'h9),
    .in8(32'h9), .in9(32'h1), .in10(32'h2), .in11(32'h2), .out(multiplexer_1_out), .sel(icode));  // open: in12, in13, in14, in15
  _1__jle u_1_jle_1 (.SF(sf), .ZF(zf), .OF(of), .out_4(n1_jle_1_out_4));
  _2_JL u_2_jl_1 (.of(undriven), .out_3(sf), .SF(of));
  Adder #(.width(32)) adder_1 (.a(multiplexer_1_out), .b(PC), .out(valP));  // open: cin, cout
  Multiplexer #(.width(32), .enable("false")) multiplexer_2 (
    .in0(valP), .in1(valC), .out(multiplexer_2_out), .sel(multiplexer_3_out));
  Multiplexer #(.select(4), .enable("false")) multiplexer_3 (
    .in0(1'b1), .in1(n1_jle_1_out_4), .in2(undriven), .in3(of), .in4(not_1_out), .in5(n5_jge_1_out_3),
    .in6(n6_jg_1_out_4), .out(multiplexer_3_out), .sel(ifun));  // open: in7, in8, in9, in10, in11, in12, in13, in14, in15
  not not_1 (not_1_out, zf);
  _5_jge u_5_jge_1 (.SF(sf), .out_3(n5_jge_1_out_3), .OF(of));
  _6_jg u_6_jg_1 (.sf(sf), ._0f(of), .zf(zf), .out_4(n6_jg_1_out_4));
  Multiplexer #(.select(4), .width(32), .enable("false")) multiplexer_4 (
    .in0(valP), .in1(valP), .in2(valP), .in3(valP), .in4(valP), .in5(valP), .in6(valP),
    .in7(multiplexer_2_out), .in8(valC), .in9(valM), .in10(valP), .in11(valP), .out(New_PC), .sel(icode));  // open: in12, in13, in14, in15

  // Other names for the same wires on the sheet: valC_0[31:0] = valC

  // Notes on the sheet:
  //   PC Increment
  //   Input: icode, PC
  //   Output: The next value for PC, or Val P
  //   PC + Instruction Length
endmodule

module srcA (
  input  [3:0] rA,
  input  [3:0] icode,
  output [3:0] srcA
);

  Multiplexer #(.select(4), .width(4), .enable("false")) multiplexer_1 (
    .in0(4'b1111), .in1(4'b1111), .in2(rA), .in3(4'b1111), .in4(rA), .in5(4'b1111), .in6(rA), .in7(4'b1111),
    .in8(4'b1111), .in9(4'b0100), .in10(rA), .in11(4'b0100), .out(srcA), .sel(icode));  // open: in12, in13, in14, in15
endmodule

module srcB (
  input  [3:0] in_1,
  input  [3:0] rB,
  output [3:0] out_3
);

  Multiplexer #(.select(4), .width(4), .enable("false")) multiplexer_1 (
    .in0(4'b1111), .in1(4'b1111), .in2(4'b1111), .in3(4'b1111), .in4(rB), .in5(rB), .in6(rB), .in7(4'b1111),
    .in8(4'b0100), .in9(4'b0100), .in10(4'b0100), .in11(4'b0100), .out(out_3), .sel(in_1));  // open: in12, in13, in14, in15
endmodule

module dstE (
  input  [3:0] rB,
  input  [3:0] icode,
  input  [3:0] ifun,
  input  zf,
  input  sf,
  input  of,
  output [3:0] destE
);

  wire multiplexer_1_out, n1_jle_1_out_4, n2_jl_1_out_3, n5_jge_1_out_3, n6_jg_1_out_4;
  wire [3:0] multiplexer_2_out;

  _1__jle u_1_jle_1 (.SF(sf), .ZF(zf), .OF(of), .out_4(n1_jle_1_out_4));
  _2_JL u_2_jl_1 (.of(of), .out_3(n2_jl_1_out_3), .SF(sf));
  _5_jge u_5_jge_1 (.SF(sf), .out_3(n5_jge_1_out_3), .OF(of));
  _6_jg u_6_jg_1 (.sf(sf), ._0f(of), .zf(zf), .out_4(n6_jg_1_out_4));
  Multiplexer #(.select(4), .enable("false")) multiplexer_1 (
    .in0(1'b1), .in1(n1_jle_1_out_4), .in2(n2_jl_1_out_3), .in5(n5_jge_1_out_3), .in6(n6_jg_1_out_4),
    .out(multiplexer_1_out), .sel(ifun));  // open: in3, in4, in7, in8, in9, in10, in11, in12, in13, in14, in15
  Multiplexer #(.width(4), .enable("false")) multiplexer_2 (
    .in0(4'b1111), .in1(rB), .out(multiplexer_2_out), .sel(multiplexer_1_out));
  Multiplexer #(.select(4), .width(4), .enable("false")) multiplexer_3 (
    .in0(4'b1111), .in1(4'b1111), .in2(multiplexer_2_out), .in3(rB), .in4(4'b1111), .in5(4'b1111), .in6(rB),
    .in7(4'b1111), .in8(4'b0100), .in9(4'b0100), .in10(4'b0100), .in11(4'b0100), .out(destE), .sel(icode));  // open: in12, in13, in14, in15

  // Notes on the sheet:
  //   Add register names to this mux
endmodule

module dstM (
  input  [3:0] rA,
  input  [3:0] icode,
  output [3:0] dst_M
);

  Multiplexer #(.select(4), .width(4), .enable("false")) multiplexer_1 (
    .in0(4'b1111), .in1(4'b1111), .in2(4'b1111), .in3(4'b1111), .in4(4'b1111), .in5(rA), .in6(4'b1111),
    .in7(4'b1111), .in8(4'b1111), .in9(4'b1111), .in10(4'b1111), .in11(rA), .out(dst_M), .sel(icode));  // open: in12, in13, in14, in15

  // Notes on the sheet:
  //   Add register names
endmodule

module select_aluA (
  input  [31:0] valA_0,
  input  [31:0] valA_1,
  input  [31:0] valC_0,
  input  [31:0] valC_1,
  input  [3:0] icode,
  input  [3:0] icode_2,
  output [31:0] aluA_0,
  output [31:0] aluA_1
);

  Multiplexer #(.select(4), .width(32), .enable("false")) multiplexer_1 (
    .in0({32{1'b0}}), .in1({32{1'b0}}), .in2(valA_0), .in3(valC_0), .in4(valC_0), .in5(valC_0), .in6(valA_0),
    .in7({32{1'b0}}), .in8(32'hfffffff8), .in9(32'h8), .in10(32'hfffffff8), .in11(32'h8), .out(aluA_0),
    .sel(icode));  // open: in12, in13, in14, in15
  Multiplexer #(.select(4), .width(32), .enable("false")) multiplexer_2 (
    .in0({32{1'b0}}), .in1({32{1'b0}}), .in2(valA_1), .in3(valC_1), .in4(valC_1), .in5(valC_1), .in6(valA_1),
    .in7({32{1'b0}}), .in8({32{1'b0}}), .in9({32{1'b0}}), .in10({32{1'b0}}), .in11({32{1'b0}}), .out(aluA_1),
    .sel(icode_2));  // open: in12, in13, in14, in15

  // Notes on the sheet:
  //   conflict: cmov and rmmov have the same icode but send diffent aluA values
  //   less signifcant 32 bits
  //   more signifcant 32 bits
endmodule

module select_aluB (
  input  [31:0] valB_0,
  input  [31:0] valB_1,
  input  [3:0] icode,
  input  [3:0] icode_2,
  output [31:0] aluB_0,
  output [31:0] aluB_1
);

  Multiplexer #(.select(4), .width(32), .enable("false")) multiplexer_1 (
    .in0({32{1'b0}}), .in1({32{1'b0}}), .in2({32{1'b0}}), .in3({32{1'b0}}), .in4(valB_0), .in5(valB_0),
    .in6(valB_0), .in7({32{1'b0}}), .in8(valB_0), .in9(valB_0), .in10(valB_0), .in11(valB_0), .out(aluB_0),
    .sel(icode));  // open: in12, in13, in14, in15
  Multiplexer #(.select(4), .width(32), .enable("false")) multiplexer_2 (
    .in0({32{1'b0}}), .in1({32{1'b0}}), .in2({32{1'b0}}), .in3({32{1'b0}}), .in4(valB_1), .in5(valB_1),
    .in6(valB_1), .in7({32{1'b0}}), .in8(valB_1), .in9(valB_1), .in10(valB_1), .in11(valB_1), .out(aluB_1),
    .sel(icode_2));  // open: in12, in13, in14, in15
endmodule

module select_read (
  input  [3:0] icode,
  output read
);

  Multiplexer #(.select(4), .enable("false")) multiplexer_1 (
    .in0(1'b0), .in1(1'b0), .in2(1'b0), .in3(1'b0), .in4(1'b0), .in5(1'b1), .in6(1'b1), .in7(1'b0),
    .in8(1'b0), .in9(1'b1), .in10(1'b0), .in11(1'b1), .out(read), .sel(icode));  // open: in12, in13, in14, in15

  // Notes on the sheet:
  //   Select the read command of the given instruction
endmodule

module select_write (
  input  [3:0] icode,
  output write
);

  Multiplexer #(.select(4), .enable("false")) multiplexer_1 (
    .in0(1'b0), .in1(1'b0), .in2(1'b0), .in3(1'b0), .in4(1'b1), .in5(1'b0), .in6(1'b1), .in7(1'b0),
    .in8(1'b1), .in9(1'b0), .in10(1'b1), .in11(1'b1), .out(write), .sel(icode));  // open: in12, in13, in14, in15
endmodule

module select_address (
  input  [31:0] valE_0,
  input  [31:0] valE_1,
  input  [31:0] valA_0,
  input  [3:0] icode,
  input  [31:0] valA_1,
  input  [3:0] icode_2,
  output [31:0] address_0,
  output [31:0] address_1
);

  Multiplexer #(.select(4), .width(32), .enable("false")) multiplexer_1 (
    .in0({32{1'b0}}), .in1({32{1'b0}}), .in2({32{1'b0}}), .in3(valE_0), .in4(valE_0), .in5(valE_0),
    .in6({32{1'b0}}), .in7({32{1'b0}}), .in8(valE_0), .in9(valA_0), .in10(valE_0), .in11(valA_0),
    .out(address_0), .sel(icode));  // open: in12, in13, in14, in15
  Multiplexer #(.select(4), .width(32), .enable("false")) multiplexer_2 (
    .in0({32{1'b0}}), .in1({32{1'b0}}), .in2({32{1'b0}}), .in3(valE_1), .in4(valE_1), .in5(valE_1),
    .in6({32{1'b0}}), .in7({32{1'b0}}), .in8({32{1'b0}}), .in9({32{1'b0}}), .in10({32{1'b0}}),
    .in11({32{1'b0}}), .out(address_1), .sel(icode_2));  // open: in12, in13, in14, in15
endmodule

module select_data (
  input  [31:0] valP_0,
  input  [3:0] icode,
  input  [31:0] valA_0,
  input  [31:0] valA_1,
  input  [3:0] icode_2,
  output [31:0] data_1,
  output [31:0] data_0
);

  wire [31:0] undriven;

  Multiplexer #(.select(4), .width(32), .enable("false")) multiplexer_1 (
    .in0({32{1'b0}}), .in1({32{1'b0}}), .in2({32{1'b0}}), .in3({32{1'b0}}), .in4(valA_1), .in5({32{1'b0}}),
    .in6({32{1'b0}}), .in7(undriven), .in8({32{1'b0}}), .in9({32{1'b0}}), .in10(valA_1), .in11({32{1'b0}}),
    .out(data_1), .sel(icode));  // open: in12, in13, in14, in15
  Multiplexer #(.select(4), .width(32), .enable("false")) multiplexer_2 (
    .in0({32{1'b0}}), .in1({32{1'b0}}), .in2({32{1'b0}}), .in3({32{1'b0}}), .in4(valA_0), .in5({32{1'b0}}),
    .in6({32{1'b0}}), .in7({32{1'b0}}), .in8(valP_0), .in9({32{1'b0}}), .in10(valA_0), .in11({32{1'b0}}),
    .out(data_0), .sel(icode_2));  // open: in12, in13, in14, in15
endmodule

module Status_Update (
  input  dmemError,
  input  [3:0] ifun,
  input  imemError,
  input  [3:0] icode,
  output [1:0] new_stat
);

  wire or_1_out;
  wire [1:0] checkifun, invalid_override, multiplexer_1_out, multiplexer_2_out, multiplexer_3_out,
       multiplexer_6_out;

  Multiplexer #(.select(4), .width(2), .enable("false")) multiplexer_1 (
    .in0(2'b00), .in1(2'b00), .in2(2'b00), .in3(2'b00), .in4(2'b01), .in5(2'b01), .in6(2'b01), .in7(2'b01),
    .in8(2'b01), .in9(2'b01), .in10(2'b01), .in11(2'b01), .in12(2'b01), .in13(2'b01), .in14(2'b01),
    .in15(2'b01), .out(multiplexer_1_out), .sel(ifun));
  Multiplexer #(.select(4), .width(2), .enable("false")) multiplexer_2 (
    .in0(2'b00), .in1(2'b00), .in2(2'b00), .in3(2'b00), .in4(2'b00), .in5(2'b00), .in6(2'b00), .in7(2'b01),
    .in8(2'b01), .in9(2'b01), .in10(2'b01), .in11(2'b01), .in12(2'b01), .in13(2'b01), .in14(2'b01),
    .in15(2'b01), .out(multiplexer_2_out), .sel(ifun));
  Multiplexer #(.select(4), .width(2), .enable("false")) multiplexer_3 (
    .in0(2'b11), .in1(2'b00), .in2(2'b00), .in3(2'b00), .in4(2'b00), .in5(2'b00), .in6(2'b00), .in7(2'b00),
    .in8(2'b00), .in9(2'b00), .in10(2'b00), .in11(2'b00), .in12(2'b00), .in13(2'b00), .in14(2'b00),
    .in15(2'b00), .out(multiplexer_3_out), .sel(icode));
  Multiplexer #(.select(4), .width(2), .enable("false")) multiplexer_4 (
    .in0(multiplexer_3_out), .in1(2'b01), .in2(2'b01), .in3(2'b01), .in4(2'b01), .in5(2'b01), .in6(2'b01),
    .in7(2'b01), .in8(2'b01), .in9(2'b01), .in10(2'b01), .in11(2'b01), .in12(2'b01), .in13(2'b01),
    .in14(2'b01), .in15(2'b01), .out(checkifun), .sel(ifun));
  Multiplexer #(.select(4), .width(2), .enable("false")) multiplexer_5 (
    .in0(checkifun), .in1(checkifun), .in2(checkifun), .in3(checkifun), .in4(checkifun), .in5(checkifun),
    .in6(multiplexer_1_out), .in7(multiplexer_2_out), .in8(checkifun), .in9(checkifun), .in10(checkifun),
    .in11(checkifun), .in12(2'b01), .in13(2'b01), .in14(2'b01), .in15(2'b01), .out(invalid_override),
    .sel(icode));
  or or_1 (or_1_out, dmemError, imemError);
  Multiplexer #(.width(2), .enable("false")) multiplexer_6 (
    .in0(2'b00), .in1(2'b10), .out(multiplexer_6_out), .sel(or_1_out));
  Multiplexer #(.select(2), .width(2), .enable("false")) multiplexer_7 (
    .in0(multiplexer_6_out), .in1(invalid_override), .in2(invalid_override), .in3(invalid_override),
    .out(new_stat), .sel(invalid_override));

  // Notes on the sheet:
  //   check ifun for certain instructions
  //   Checks to see if instruction is invalid by checking icode
  //   Also triggers halt if icode is 00
  //   evalulates all instructions that require an ifun of 0 to see if the ifun is 0
  //   Input:
  //   Output:
  //   00 - normal
  //   11 - halt
  //   01 - invalid instruction
  //   Status Update:
  //   icode, some memory stuff
  //   The new status of the CPU:
  //   10 - invalid memory address
endmodule

module _1__jle (
  input  SF,
  input  ZF,
  input  OF,
  output out_4
);

  wire and_1_out;

  and and_1 (and_1_out, SF, OF);
  or or_1 (out_4, and_1_out, ZF);
endmodule

module _2_JL (
  input  of,
  input  SF,
  output out_3
);

  wire and_1_out, not_1_out, or_1_out;

  and and_1 (and_1_out, SF, of);
  or or_1 (or_1_out, SF, of);
  not not_1 (not_1_out, and_1_out);
  and and_2 (out_3, not_1_out, or_1_out);
endmodule

module _5_jge (
  input  SF,
  input  OF,
  output out_3
);

  wire and_1_out;

  and and_1 (and_1_out, SF, OF);
  not not_1 (out_3, and_1_out);
endmodule

module _6_jg (
  input  sf,
  input  _0f,
  input  zf,
  output out_4
);

  wire and_1_out, not_1_out, not_2_out;

  and and_1 (and_1_out, sf, _0f);
  not not_1 (not_1_out, zf);
  not not_2 (not_2_out, and_1_out);
  and and_2 (out_4, not_2_out, not_1_out);

  // Other names for the same wires on the sheet: OF = _0f
endmodule

module set_flags (
  input  SF,
  input  OF,
  input  ZF,
  input  [3:0] icode,
  output sf_2,
  output of_2,
  output zf_2
);

  wire and_1_out, and_2_out, and_3_out, clock_1_out, clock_2_out, clock_3_out, multiplexer_1_out,
       multiplexer_2_out, multiplexer_3_out;

  and and_1 (and_1_out, clock_1_out, multiplexer_1_out);
  Clock clock_1 (.out(clock_1_out));
  Register #(.width(1)) register_1 (.D(ZF), .Q(zf_2), .clk(and_1_out));  // open: en, clr
  Multiplexer #(.select(4), .enable("false")) multiplexer_1 (
    .in0(1'b0), .in1(1'b0), .in2(1'b0), .in3(1'b0), .in4(1'b0), .in5(1'b0), .in6(1'b1), .in7(1'b0),
    .in8(1'b0), .in9(1'b0), .in10(1'b0), .out(multiplexer_1_out), .sel(icode));  // open: in11, in12, in13, in14, in15
  Register #(.width(1)) register_2 (.D(SF), .Q(sf_2), .clk(and_2_out));  // open: en, clr
  and and_2 (and_2_out, clock_2_out, multiplexer_2_out);
  Clock clock_2 (.out(clock_2_out));
  Multiplexer #(.select(4), .enable("false")) multiplexer_2 (
    .in0(1'b0), .in1(1'b0), .in2(1'b0), .in3(1'b0), .in4(1'b0), .in5(1'b0), .in6(1'b1), .in7(1'b0),
    .in8(1'b0), .in9(1'b0), .in10(1'b0), .out(multiplexer_2_out), .sel(icode));  // open: in11, in12, in13, in14, in15
  Register #(.width(1)) register_3 (.D(OF), .Q(of_2), .clk(and_3_out));  // open: en, clr
  and and_3 (and_3_out, clock_3_out, multiplexer_3_out);
  Clock clock_3 (.out(clock_3_out));
  Multiplexer #(.select(4), .enable("false")) multiplexer_3 (
    .in0(1'b0), .in1(1'b0), .in2(1'b0), .in3(1'b0), .in4(1'b0), .in5(1'b0), .in6(1'b1), .in7(1'b0),
    .in8(1'b0), .in9(1'b0), .in10(1'b0), .out(multiplexer_3_out), .sel(icode));  // open: in11, in12, in13, in14, in15
endmodule

module B1 (
  input  [7:0] B1,
  output [3:0] icode
);

  Multiplexer #(.select(4), .width(8), .enable("false")) multiplexer_1 (
    .in2(B1), .sel(icode));  // open: in0, in1, in3, in4, in5, in6, in7, in8, in9, in10, in11, in12, in13, in14, in15, out
endmodule

module need_reg (
  input  [3:0] icode,
  output NeedRegs
);

  Multiplexer #(.select(4)) multiplexer_1 (
    .in0(1'b0), .in1(1'b0), .in2(1'b1), .in3(1'b1), .in4(1'b1), .in5(1'b1), .in6(1'b1), .in7(1'b0),
    .in8(1'b0), .in9(1'b0), .in10(1'b1), .in11(1'b1), .in12(1'b1), .in13(1'b1), .in14(1'b1), .in15(1'b1),
    .out(NeedRegs), .sel(icode));  // open: en
endmodule
